# Fritzing sketch Circuit_Diagrams_schem (saved by Fritzing 0.9.3b)
breadboards: 1

parts:
  Part1 = Arduino Board Ethernet
  R1 = Resistor [tolerance=±5% resistance=220 package=THT]
  R2 = Resistor [tolerance=±5% resistance=220 package=THT]
  R3 = Resistor [tolerance=±5% resistance=220 package=THT]
  R4 = Resistor [tolerance=±5% resistance=220 package=THT]
  R5 = Resistor [tolerance=±5% resistance=220 package=THT]
  R6 = Resistor [tolerance=±5% resistance=220 package=THT]
  Side_Street = LED - 5mm [color="Red (633nm)" package="5 mm [THT]"]
  Main_Street = LED - 5mm [color="Red (633nm)" package="5 mm [THT]"]
  Main_Street_2 = LED - 5mm [color="Green (555nm)" package="5 mm [THT]"]
  Side_Street_2 = LED - 5mm [color="Green (555nm)" package="5 mm [THT]"]
  Main_Street_3 = LED - 5mm [color="Yellow (595nm)" package="5 mm [THT]"]
  Side_Street_3 = LED - 5mm [color="Yellow (595nm)" package="5 mm [THT]"]

nets:
  N1: Part1.D2_PWM, Side_Street_2.cathode
  N2: Part1.D3_PWM, Side_Street_3.cathode
  N3: Part1.D4, Side_Street.cathode
  N4: Part1.D5_PWM, Main_Street_2.cathode
  N5: Part1.D6_PWM, Main_Street_3.cathode
  N6: Part1.D7, Main_Street.cathode
  N7: Part1.GND, R1.Pin_0, R2.Pin_0, R3.Pin_0, R4.Pin_0, R5.Pin_0, R6.Pin_0
  N8: R1.Pin_1, Main_Street_3.anode
  N9: R2.Pin_1, Main_Street_2.anode
  N10: R3.Pin_1, Side_Street.anode
  N11: R4.Pin_1, Side_Street_3.anode
  N12: R5.Pin_1, Side_Street_2.anode
  N13: R6.Pin_1, Main_Street.anode
