# Fritzing sketch Lab3_Circuit2 (saved by Fritzing 0.9.3b)
breadboards: 1

parts:
  Part1 = Arduino Board Ethernet
  R17 = Rotary Potentiometer (Small) [maximum_resistance=100kΩ package=THT]
  LCD1 = LCD screen
  R18 = Rotary Potentiometer (Small) [maximum_resistance=100kΩ package=THT]

nets:
  N1: Part1.D8, LCD1.DB4
  N2: Part1.D9_PWM, LCD1.DB5
  N3: Part1.D10_PWM/SS, LCD1.DB6
  N4: Part1.D11/MOSI, LCD1.DB7
  GND: Part1.GND, R17.leg1, LCD1.VSS, LCD1.LED-, R18.leg1
  N5: Part1.A0, R18.wiper
  N6: Part1.D0/RX, LCD1.RS
  N7: Part1.D1/TX, Part1.PD1, LCD1.E
  N8: Part1.D6_PWM, LCD1.R/W
  5V: Part1.5V, R17.leg2, LCD1.VDD, R18.leg2
  N9: R17.wiper, LCD1.V0
