# Fritzing sketch Lab3_Circuit3 (saved by Fritzing 0.9.3b)
breadboards: 1

parts:
  Part1 = Arduino Board Ethernet
  R1 = Resistor [tolerance=±5% resistance=220 package=THT]
  R2 = Resistor [tolerance=±5% resistance=220 package=THT]
  R3 = Resistor [tolerance=±5% resistance=220 package=THT]
  R4 = Resistor [tolerance=±5% resistance=220 package=THT]
  R5 = Resistor [tolerance=±5% resistance=220 package=THT]
  R6 = Resistor [tolerance=±5% resistance=220 package=THT]
  R7 = Resistor [tolerance=±5% resistance=220 package=THT]
  R8 = Resistor [tolerance=±5% resistance=220 package=THT]
  R9 = Resistor [tolerance=±5% resistance=220 package=THT]
  R10 = Resistor [tolerance=±5% resistance=220 package=THT]
  R11 = Resistor [tolerance=±5% resistance=220 package=THT]
  R12 = Resistor [tolerance=±5% resistance=220 package=THT]
  LED1 = 7-SEGMENT-4DIGIT-YOUNGSUN [package=7-segment-4digit-youngsun-longpads]
  R13 = Rotary Potentiometer (Small) [maximum_resistance=100kΩ package=THT]

nets:
  N1: Part1.D8, R2.Pin_1
  N2: Part1.D9_PWM, R9.Pin_1
  N3: Part1.D10_PWM/SS, R10.Pin_1
  N4: Part1.D11/MOSI, R11.Pin_1
  N5: Part1.A0, R13.wiper
  N6: Part1.D2_PWM, R3.Pin_0
  N7: Part1.D3_PWM, R12.Pin_0
  N8: Part1.D4, R1.Pin_1
  N9: Part1.D5_PWM, R4.Pin_1
  N10: Part1.D6_PWM, R7.Pin_1
  N11: Part1.D7, R8.Pin_1
  N12: Part1.GND, R13.leg1
  N13: Part1.5V, R13.leg2
  N14: Part1.PD0, R6.Pin_1
  N15: Part1.PD1, R5.Pin_1
  N16: R1.Pin_0, LED1.D
  N17: R2.Pin_0, LED1.DIG4
  N18: R3.Pin_1, LED1.F
  N19: R4.Pin_0, LED1.C
  N20: R5.Pin_0, LED1.G
  N21: R6.Pin_0, LED1.DP
  N22: R7.Pin_0, LED1.B
  N23: R8.Pin_0, LED1.A
  N24: R9.Pin_0, LED1.DIG3
  N25: R10.Pin_0, LED1.DIG2
  N26: R11.Pin_0, LED1.DIG1
  N27: R12.Pin_1, LED1.E
