# Fritzing sketch lab3_circuit1 (saved by Fritzing 0.9.3b)
breadboards: 1

parts:
  R1 = Resistor [tolerance=±5% resistance=220 package=THT]
  Part1 = Arduino Board Ethernet
  U1 = 7-SEGMENT-DISPLAY-1_-RED [package=7-segment-1_pth]
  R9 = Resistor [tolerance=±5% resistance=220 package=THT]
  R10 = Resistor [tolerance=±5% resistance=220 package=THT]
  R11 = Resistor [tolerance=±5% resistance=220 package=THT]
  R12 = Resistor [tolerance=±5% resistance=220 package=THT]
  R13 = Resistor [tolerance=±5% resistance=220 package=THT]
  R14 = Resistor [tolerance=±5% resistance=220 package=THT]
  R15 = Resistor [tolerance=±5% resistance=220 package=THT]
  R16 = Resistor [tolerance=±5% resistance=220 package=THT]  # not connected

nets:
  N1: R1.Pin_0, Part1.PD0
  N2: R1.Pin_1, U1.DP
  N3: Part1.D2_PWM, R11.Pin_0
  N4: Part1.D3_PWM, R10.Pin_0
  N5: Part1.D4, R15.Pin_1
  N6: Part1.D5_PWM, R13.Pin_1
  N7: Part1.D6_PWM, R14.Pin_1
  N8: Part1.D7, R12.Pin_1
  N9: Part1.PD1, R9.Pin_0
  N10: Part1.GND, U1.G1, U1.G2
  N11: U1.E, R10.Pin_1
  N12: U1.D, R15.Pin_0
  N13: U1.C, R13.Pin_0
  N14: U1.B, R14.Pin_0
  N15: U1.A, R12.Pin_0
  N16: U1.F, R11.Pin_1
  N17: U1.G, R9.Pin_1
